# Fritzing sketch frit POV 3 sketch (saved by Fritzing 0.9.3b)
circuit board: 27.9882cm x 1.55cm
circuit board: 5.98306cm x 1.77434cm
circuit board: 27.9933cm x 2.05cm
breadboards: 1

parts:
  J1 = female pin header, 14 pins [form="♀ (female)"]
  J2 = female pin header, 14 pins [form="♀ (female)"]
  Gn_14_7_5v = female pin header, 4 pins [form="♀ (female)"]
  V5_7_14_Gn = female pin header, 4 pins [form="♀ (female)"]
  Gnd_5V = female pin header, 3 pins [form="♀ (female)"]
  J1_2 = female pin header, 4 pins [form="♀ (female)"]
  J4 = female pin header, 4 pins [form="♀ (female)"]
  J8 = female pin header, 4 pins [form="♀ (female)"]
  J9 = female pin header, 4 pins [form="♀ (female)"]
  J10 = female pin header, 4 pins [form="♀ (female)"]
  J11 = female pin header, 4 pins [form="♀ (female)"]
  J2_2 = female pin header, 4 pins [form="♀ (female)"]
  J3 = female pin header, 4 pins [form="♀ (female)"]
  J5 = female pin header, 4 pins [form="♀ (female)"]
  J6 = female pin header, 4 pins [form="♀ (female)"]
  J7 = female pin header, 4 pins [form="♀ (female)"]
  J8_2 = female pin header, 4 pins [form="♀ (female)"]
  328p = Arduino Nano (Rev3.0)
  D3 = female pin header, 3 pins [form="♀ (female)"]
  D4 = female pin header, 3 pins [form="♀ (female)"]
  D5 = female pin header, 3 pins [form="♀ (female)"]
  D6 = female pin header, 3 pins [form="♀ (female)"]
  D7 = female pin header, 3 pins [form="♀ (female)"]
  Gnd_5V_2 = female pin header, 2 pins [form="♀ (female)"]
  Gnd_D13 = female pin header, 2 pins [form="♀ (female)"]

nets:
  N1: J1.pin2, Gn_14_7_5v.pin3, V5_7_14_Gn.pin2, J8.pin3, J9.pin3, J10.pin2, J11.pin2
  N2: J1.pin14, Gn_14_7_5v.pin1, V5_7_14_Gn.pin4, Gnd_5V.pin3, J8.pin1, J9.pin1, J10.pin4, J11.pin4
  N3: J2.pin6, Gn_14_7_5v.pin2, V5_7_14_Gn.pin3, J8.pin2, J9.pin2, J10.pin3, J11.pin3
  N4: J2.pin14, Gn_14_7_5v.pin4, V5_7_14_Gn.pin1, Gnd_5V.pin1, J8.pin4, J9.pin4, J10.pin1, J11.pin1
  N5: J1_2.pin1, J2_2.pin1, J3.pin1, J7.pin1
  N6: J1_2.pin2, J2_2.pin2, J3.pin2, J7.pin2
  N7: J1_2.pin3, J2_2.pin3, J3.pin3, J7.pin3
  N8: J1_2.pin4, J2_2.pin4, J3.pin4, J7.pin4
  N9: J4.pin1, J5.pin1
  N10: J4.pin2, J5.pin2, J6.pin2, J8_2.pin2
  N11: J4.pin3, J5.pin3, J6.pin3, J8_2.pin3
  N12: J4.pin4, J5.pin4, J6.pin4, J8_2.pin4
  N13: J6.pin1, J8_2.pin1
  N14: 328p.GND, D3.pin1, D4.pin1, D5.pin1, D6.pin1, D7.pin1, Gnd_5V_2.pin2, Gnd_D13.pin2
  N15: 328p.D3, D3.pin3
  N16: 328p.D4, D4.pin3
  N17: 328p.D5, D5.pin3
  N18: 328p.D6, D6.pin3
  N19: 328p.D7, D7.pin3
  N20: 328p.VIN, D3.pin2, D4.pin2, D5.pin2, D6.pin2, D7.pin2, Gnd_5V_2.pin1
  N21: 328p.D13/SCK, Gnd_D13.pin1

notes:
  Synerflight POV
